# Fritzing sketch SmartHomeTempSensor (saved by Fritzing 0.9.3b)
circuit board: 4.43196cm x 5.69405cm
breadboards: 1

parts:
  M1 = STM32F103C8T6 blue mini board
  VCC1 = Battery block 9V
  J1 = Piezo Speaker
  R1 = Resistor [tolerance=±5% resistance=220 package=THT]
  U1 = Voltage Regulator - Variable [package="TO220 [THT]"]
  J2 = female alternating pin header, 2 pins [form="♀ (female)"]

nets:
  N1: M1.G, VCC1.-, J1.pin1, R1.Pin_0, U1.OUT
  N2: M1.A0, R1.Pin_1, J2.pin2
  N3: M1.A1, J1.pin2
  N4: VCC1.+, U1.ADJ
  N5: U1.IN, J2.pin1

notes:
  Adrian De Braga
